# Fritzing sketch debounce (saved by Fritzing 0.8.7b)
breadboards: 1

parts:
  Componente2 = Arduino Pro Mini v13
  C1 = Ceramic Capacitor [capacitance=5nF package="100 mil [THT, multilayer]"]
  R1 = Resistor [tolerance=±5% resistance=680k package=THT]
  R2 = Resistor [tolerance=±5% resistance=680k package=THT]
  S1 = Pushbutton [package="[THT]"]

nets:
  N1: Componente2.GND, R2.Pin_1
  N2: Componente2.VCC, C1.0, S1.Pin_3, S1.Pin_4
  N3: Componente2.D2, R1.Pin_1, R2.Pin_0, S1.Pin_1, S1.Pin_2
  N4: C1.1, R1.Pin_0
