# Fritzing sketch smartrail (saved by Fritzing 0.8.7b)
breadboards: 1

parts:
  M1 = Stepper Motor - Bipolar
  Componente1 = EasyDriver_v44
  Componente2 = Arduino Pro Mini v13
  Componente3 = Thumb Joystick
  Componente4 = Thumb Joystick
  M2 = Stepper Motor - Bipolar
  Componente5 = EasyDriver_v44
  M3 = Stepper Motor - Bipolar
  Componente6 = EasyDriver_v44
  S1 = SWITCH-MOMENTARY-2 [package=tactile-switch-1101ne]
  S2 = SWITCH-MOMENTARY-2 [package=tactile-switch-1101ne]
  U1 = LIPO-2000mAh [package=lipo-2000]
  J1 = Basic Servo
  J2 = Basic Servo

nets (from the breadboard view):
  N1: M1.A, Componente1.OUT2A
  N2: M1.C, Componente1.OUT2B
  N3: M1.B, Componente1.OUT1A
  N4: M1.D, Componente1.OUT1B
  GND: Componente1.GND, Componente2.GND, Componente3.GND, Componente4.GND, Componente5.GND, Componente6.GND, S1.1, S2.1, U1.-, J1.gnd, J2.gnd
  N5: Componente1.V+, Componente5.V+, Componente6.V+, U1.+
  N6: Componente1.STEP, Componente2.D9_PWM
  N7: Componente1.DIR, Componente2.D8
  VCC: Componente1.VCC, Componente2.VCC, Componente3.VCC, Componente4.VCC, Componente5.VCC, Componente6.VCC, J1.vcc, J2.vcc
  N8: Componente2.A4, Componente3.HORZ
  N9: Componente2.A5, Componente3.VERT
  N10: Componente2.A3, Componente4.VERT
  N11: Componente2.A2, Componente4.HORZ
  N12: Componente2.D13/SCK, J2.pulse
  N13: Componente2.D12/MISO, J1.pulse
  N14: Componente2.D11_PWM/MOSI, Componente6.DIR
  N15: Componente2.D10_PWM/SS, Componente6.STEP
  N16: Componente2.D7, Componente5.STEP
  N17: Componente2.D6_PWM, Componente5.DIR
  N18: Componente2.D4, Componente4.SEL
  N19: Componente2.D3_PWM, S1.2, S2.2
  N20: Componente2.D2, Componente3.SEL
  N21: M2.A, Componente5.OUT2A
  N22: M2.C, Componente5.OUT2B
  N23: M2.B, Componente5.OUT1A
  N24: M2.D, Componente5.OUT1B
  N25: M3.A, Componente6.OUT2A
  N26: M3.C, Componente6.OUT2B
  N27: M3.B, Componente6.OUT1A
  N28: M3.D, Componente6.OUT1B
